# Fritzing sketch smartVase (saved by Fritzing 1.0.2b)
breadboards: 1

parts:
  U1 = ESP32-38PinWide [part_number=ESP32-38PinWide]
  HC-SR04_Sensor_1 = HC-SR04 Ultrasonic Distance Sensor
  SP1 = SPEAKER [package=pcb_mount_speaker]
  Bauteil2 = FC-28 Soil Hygrometer Module - Probe
  Bauteil3 = FC-28 Soil Hygrometer Module
  Mini_Water_Pump_3-6VDC1 = Mini Water Pump 3-6VDC [part_number="Mini Water Pump 3-6VDC" chip_label=IC package="DIP (Dual Inline) [THT]"]
  DHT1 = DHT11 Humitidy and Temperature Sensor (3 pins)
  Water_Level_Sensor1 = Water Level Sensor
  L298N1 = L298N DC motor driver

nets:
  N1: U1.3.3, SP1.-
  N2: U1.GPIO34, Bauteil3.AO
  N3: U1.GPIO35, Water_Level_Sensor1.SIG
  N4: U1.GPIO33, L298N1.IN2
  N5: U1.GPIO25, L298N1.IN1
  GND: U1.GND, HC-SR04_Sensor_1.GND, Bauteil3.GND, DHT1.Gnd, Water_Level_Sensor1.GND, L298N1.GND
  VCC: U1.VIN, HC-SR04_Sensor_1.VCC, Bauteil3.VCC, DHT1.Plus, Water_Level_Sensor1.VCC, L298N1.12V
  N6: U1.GPIO4, SP1.+
  N7: U1.GPIO18, HC-SR04_Sensor_1.ECHO
  N8: U1.GPIO19, HC-SR04_Sensor_1.TRIG
  N9: U1.GPIO21, DHT1.Signal
  N10: Bauteil2.POS, Bauteil3.POS
  N11: Bauteil2.NEG, Bauteil3.NEG
  N12: Mini_Water_Pump_3-6VDC1.+M, L298N1.OUT2
  N13: Mini_Water_Pump_3-6VDC1.-M, L298N1.OUT1
  N14: L298N1.5V#9, L298N1.ENA
  N15: L298N1.5V#10, L298N1.ENB

custom parts:
  ESP32-38PinWide: Generic 38-Pin ESP32 with wide format (only access to one side of pins on a breadboard) based on Stephen Lilley's HiLetgo ESP-WROOM-32 ESP32 ESP-32S Development Board.
  FC-28 Soil Hygrometer Module - Probe: The FC-28 is a soil hygrometer module that uses the Texas Instruments LM393 comparator chip to provide an analog measurement of soil humidity.
  FC-28 Soil Hygrometer Module: The FC-28 is a soil hygrometer module that uses the Texas Instruments LM393 comparator chip to provide an analog measurement of soil humidity. The digital output is high when soil moisture is over a certain threshold, as determined by adjusting the potentiometer.
  DHT11 Humitidy and Temperature Sensor (3 pins): DHT11 Humidity and Temperature Sensor (3 pins).
  Water Level Sensor: A water level sensor. This sensor operates at 3V to 5V. The Sig (signal) pin outputs an analogue signal that is in proportion to the amount of water in contact with the sensor.
  L298N DC motor driver: 2x DC motor driver with 78M05 positive voltage regulator (7..35 V) L298N: max 46 V, 2 A Set 5 V Enable jumper to enable 5 V regultor (needed for the L298N) and +5 V output at screw terminal or supply external +5 V at screw terminal Set ENA and/or ENB to +5 V to enable motor permanently or supply ENA and/or ENB with PWM signal IN1 and IN2 set rotation directory for motor A (OUT1/OUT2) IN2 and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
